# Fritzing sketch Temperature Sensor (saved by Fritzing 0.9.3b)
breadboards: 1

parts:
  Part1 = Arduino Leonardo (Rev3b)
  LM35_Temperature_Sensor = LM35 Temperature Sensor [package="TO92 [THT]"]

nets:
  N1: Part1.5V, LM35_Temperature_Sensor.+Vs
  GND: Part1.GND, LM35_Temperature_Sensor.GND
  N2: Part1.A0, LM35_Temperature_Sensor.Vout
