# Fritzing sketch Tumbler Controller (saved by Fritzing 0.9.1b)
breadboards: 1

parts:
  Part1 = Arduino Leonardo (Rev3b)
  LED1 = smd LED [color="Red (633nm)" package="0603 [SMD]"]
  R1 = Resistor [tolerance=±5% resistance=220 package=THT]
  J1 = Piezo Speaker
  VCC1 = Battery block 9V
  IC1 = L293D [package=THT]

nets:
  N1: Part1.D2/SDA, IC1.In_1
  N2: Part1.D3_PWM/SCL, IC1.In_2
  N3: Part1.D4/A6, IC1.In_3
  N4: Part1.D5_PWM, IC1.In_4
  N5: Part1.D6_PWM/A7, J1.pin2
  N6: Part1.5V, IC1.+V
  N7: Part1.GND, R1.Pin_0, J1.pin1, VCC1.-, IC1.0V
  N8: Part1.VIN, VCC1.+
  N9: Part1.D10_PWM/A10, IC1.Enable_1
  N10: Part1.D11_PWM, IC1.Enable_2
  N11: Part1.D13_PWM, LED1.anode
  N12: LED1.cathode, R1.Pin_1
